# Fritzing sketch basementLaundryCrawlFan-ESP32 (saved by Fritzing 0.9.10b)
breadboards: 1

parts:
  5VDC_2_0A = HLK-PM01 [mpn="5VDC Power Supply" mn="DVE Switching Adapter" part_number=DSA-0101F-05A]
  ESP32 = DOIT Esp32 DevKit v1 (30 pins long, 11 pins width) [part_number=ESP32S-PIN36 mpn="ESP32 DEV v1"]
  5-15R_receptacle = 120V duplex outlet_1
  5-15P_to_barewire_cable = screw terminal, 3 pins
  115VAC_Fan = Fan - Ventilador [mpn=NMB-MAT part_number=4715MS-12T-B40 package=THT]
  F2 = Fan - Ventilador [package=THT]
  5VDC_Relay = Jtron 1 Channel Optoisolated Relay Module [mn="Tonling 5VDC" mpn=JCQ-3FF-S-Z package=relay]
  orange_wire_nut = Header 3 [package=molex-1x3_lock]
  orange_wire_nut_2 = Header 3 [package=molex-1x3_lock]

nets:
  GND: 5VDC_2_0A.-Vo, ESP32.GND, 5VDC_Relay.GND
  VIN: 5VDC_2_0A.+Vo, ESP32.VIN, 5VDC_Relay.VCC
  N1: ESP32.D32, 5VDC_Relay.IN1
  N2: 5-15R_receptacle.H1, 5-15P_to_barewire_cable.pin3
  N3: 5-15R_receptacle.H2, 5VDC_Relay.MAIN
  N4: 5-15R_receptacle.G, 5-15P_to_barewire_cable.pin2
  N5: 5-15R_receptacle.N2, orange_wire_nut.3
  N6: 5-15R_receptacle.N1, 5-15P_to_barewire_cable.pin1
  N7: 115VAC_Fan.5V, orange_wire_nut_2.2
  N8: 115VAC_Fan.GND, orange_wire_nut.1
  N9: F2.5V, orange_wire_nut_2.3
  N10: F2.GND, orange_wire_nut.2
  N11: 5VDC_Relay.NO, orange_wire_nut_2.1

notes:
  inside high voltage box
  PG9 Cable Gland
  PG11 Cable Gland
  Box Hole

custom parts:
  DOIT Esp32 DevKit v1 (30 pins long, 11 pins width): The DOIT Esp32 DevKit v1 is one of the development board created by DOIT to evaluate the ESP-WROOM-32 module. It is based on the ESP32 microcontroller that boasts Wifi, Bluetooth, Ethernet and Low Power support all in a single chip. (vanepp) made breadboard work, adjusted pin numbering and labels and reduced size of schematic and cleaned up pcb. This chip is 30pins long (2 x15) and 11 pins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
  120V duplex outlet_1: 120V duplex outlet.
  Fan - Ventilador: Ventilador de 2 pines, se encuentra comunmente en computadoras de escritorio
